# Fritzing sketch MAX485_RS-485_Module (saved by Fritzing 0.9.3b)
circuit board: 6cm x 1.99729cm
breadboards: 1
perfboards: 1

parts:
  J3 = male pin header, 4 pins [form="♂ (male)"]
  Q1 = MOSFET-NCHANNEL [part_number=FDN359AN package=sot23-3]
  R2 = Resistor [tolerance=±5% resistance=10k package=THT]
  R3 = Resistor [tolerance=±5% resistance=120 package=THT]
  R1 = Resistor [tolerance=±5% resistance=10k package=THT]
  JP1 = male pin header, 2 pins [form="♂ (male)"]
  J2 = male pin header, 4 pins [form="♂ (male)"]
  J1 = molex pin header, 4 pins [form=molex]

nets:
  5V: J3.pin1, R2.Pin_1, J1.pin2
  N1: J3.pin2, JP1.pin1
  N2: J3.pin3, R3.Pin_0
  GND: J3.pin4, Q1.S, J1.pin1
  N3: Q1.G, R1.Pin_0
  N4: Q1.D, R2.Pin_0, J2.pin2, J2.pin3
  N5: R3.Pin_1, JP1.pin2
  N6: R1.Pin_1, J2.pin4, J1.pin3
  N7: J2.pin1, J1.pin4

notes:
  RS485 LC Electronic
  RS485 Module
